# Fritzing sketch bauplan (saved by Fritzing 0.9.3b)
circuit board: 21.429cm x 10.0695cm
breadboards: 1

parts:
  Bauteil1 = Arduino Uno (Rev3)
  LCD1 = LCD screen
  DHT1 = DHT22 Humidity and Temperature Sensor
  R1 = Resistor [tolerance=±5% resistance=10 package=THT]
  LCM1602_IIC1 = LCM1602 IIC [part_number="LCM1602 IIC" chip_label="LCM1602 IIC" package="DIP (Dual Inline) [THT]"]
  Q1 = NPN-Transistor [package="TO92 [THT]"]
  LED1 = LED - 3mm [color="Red (633nm)" package="3 mm [THT]"]
  R2 = Resistor [tolerance=±5% resistance=150 package="0603 [SMD]"]
  DS1 = DS18B20 1-Wire Temperature Sensor [part_number=DS18B20]
  R3 = Resistor [tolerance=±5% resistance=4.7 package="0603 [SMD]"]
  S1 = SPST Switch [package=switch-spdt_kit]
  R4 = Resistor [tolerance=±5% resistance=150 package="0603 [SMD]"]

nets:
  N1: Bauteil1.A4/SDA, LCM1602_IIC1.SDA
  N2: Bauteil1.A5/SCL, LCM1602_IIC1.SCL
  N3: Bauteil1.D2, DHT1.DATA, S1.O
  N4: Bauteil1.D4, Q1.B
  N5: Bauteil1.D5_PWM, S1.S, R4.Pin_1
  N6: Bauteil1.D6_PWM, DS1.DQ, R3.Pin_0
  VDD: Bauteil1.5V, DHT1.VDD, R1.Pin_1, DS1.VDD, R3.Pin_1
  GND: Bauteil1.GND, DHT1.GND, DS1.GND, R4.Pin_0
  VSS: LCD1.VSS, LCM1602_IIC1.VSS
  VDD_2: LCD1.VDD, LCM1602_IIC1.VDD
  N7: LCD1.V0, LCM1602_IIC1.V0
  N8: LCD1.RS, LCM1602_IIC1.RS
  N9: LCD1.R/W, LCM1602_IIC1.RW
  N10: LCD1.E, LCM1602_IIC1.E
  N11: LCD1.DB0, LCM1602_IIC1.D0
  N12: LCD1.DB1, LCM1602_IIC1.D1
  N13: LCD1.DB2, LCM1602_IIC1.D2
  N14: LCD1.DB3, LCM1602_IIC1.D3
  N15: LCD1.DB4, LCM1602_IIC1.D4
  N16: LCD1.DB5, LCM1602_IIC1.D5
  N17: LCD1.DB6, LCM1602_IIC1.D6
  N18: LCD1.DB7, LCM1602_IIC1.D7
  N19: LCD1.LED+, LCM1602_IIC1.A
  N20: LCD1.LED-, LCM1602_IIC1.K
  N21: LCM1602_IIC1.GND, Q1.E
  N22: LCM1602_IIC1.VCC, R2.Pin_0, S1.P
  N23: LCM1602_IIC1.LED_A, LCM1602_IIC1.LED_B
  N24: Q1.C, LED1.cathode
  N25: LED1.anode, R2.Pin_1

custom parts:
  LCM1602 IIC: I2C-Module to use a 1602 or 2004 LCD on with the wire.h libory Serial LCD Modul
